# Fritzing sketch AlarmClock (saved by Fritzing 0.9.2b)
breadboards: 1

parts:
  DI1 = 7-Segment LED Display [package=THT]
  DI2 = 7-Segment LED Display [package=THT]
  DI3 = 7-Segment LED Display [package=THT]
  DI4 = 7-Segment LED Display [package=THT]
  DI5 = 7-Segment LED Display [package=THT]
  DI6 = 7-Segment LED Display [package=THT]
  Part1 = Arduino Mega ADK (Rev3)

nets:
  N1: DI1.commAnode, DI2.commAnode, DI3.commAnode, DI4.commAnode, DI5.commAnode, DI6.commAnode, Part1.GND
  N2: DI2.cathodeE, Part1.D53/SS
  N3: DI2.cathodeD, Part1.D51/MOSI
  N4: DI2.cathodeDP, Part1.D49
  N5: DI2.cathodeB, Part1.D47
  N6: DI2.cathodeA, Part1.D45
  N7: DI2.cathodeF, Part1.D50/MISO
  N8: DI2.cathodeG, Part1.D52/SCK
