# Fritzing sketch CountdownTimer (saved by Fritzing 0.9.3b)
breadboards: 1

parts:
  DI1 = 7-Segment LED Display [package=THT]
  DI2 = 7-Segment LED Display [package=THT]
  DI3 = 7-Segment LED Display [package=THT]
  DI4 = 7-Segment LED Display [package=THT]
  DI5 = 7-Segment LED Display [package=THT]
  DI6 = 7-Segment LED Display [package=THT]
  Part1 = Arduino Uno (Rev3)  # not connected

nets:
  N1: DI1.cathodeG, DI2.cathodeG, DI3.cathodeG, DI4.cathodeG, DI5.cathodeG, DI6.cathodeG
