# Fritzing sketch DigitalClock (saved by Fritzing 0.9.3b)
breadboards: 1

parts:
  DI1 = 7-Segment LED Display [package=THT]
  DI2 = 7-Segment LED Display [package=THT]
  DI3 = 7-Segment LED Display [package=THT]
  DI4 = 7-Segment LED Display [package=THT]
  DI5 = 7-Segment LED Display [package=THT]
  DI6 = 7-Segment LED Display [package=THT]
  Part1 = Arduino Uno (Rev3)
  J1 = Piezo Speaker

nets:
  N1: DI1.cathodeE, DI5.cathodeE, DI6.cathodeE
  N2: DI1.cathodeD, DI5.cathodeD, DI6.cathodeD
  N3: DI1.cathodeC, DI5.cathodeC, DI6.cathodeC
  N4: DI1.cathodeDP, DI5.cathodeDP, DI6.cathodeDP
  N5: DI2.cathodeE, Part1.D6_PWM
  N6: DI2.cathodeD, Part1.D5_PWM
  N7: DI2.cathodeC, Part1.D4
  N8: DI2.cathodeB, Part1.D3_PWM
  N9: DI2.cathodeA, Part1.D2
  N10: DI2.cathodeF, Part1.D7
  N11: DI2.cathodeG, Part1.D8
  N12: DI3.commAnode#2, Part1.D10_PWM/SS
  N13: DI4.commAnode#2, Part1.D11_PWM/MOSI
  N14: DI4.cathodeB, DI5.cathodeB, DI6.cathodeB
  N15: DI4.cathodeA, DI5.cathodeA, DI6.cathodeA
  N16: DI4.cathodeF, DI5.cathodeF, DI6.cathodeF
  N17: DI4.cathodeG, DI5.cathodeG, DI6.cathodeG
  N18: DI5.commAnode#2, Part1.D12/MISO
  N19: DI6.commAnode#2, Part1.D13/SCK
  N20: Part1.D9_PWM, J1.pin2
  N21: Part1.GND, J1.pin1
